# Fritzing sketch 5 Servos with Potentiometer 1 (saved by Fritzing 0.8.7b)
breadboards: 1

parts:
  J1 = Basic Servo
  J2 = Basic Servo
  J3 = Basic Servo
  J4 = Basic Servo
  J5 = Basic Servo
  Part1 = Arduino Uno (Rev3)
  U1 = LIPO-1000mAh [package=lipo-1000]
  R1 = Rotary Potentiometer (Small) [maximum_resistance=100kΩ package=THT]
  R2 = Rotary Potentiometer (Small) [maximum_resistance=100kΩ package=THT]
  R3 = Rotary Potentiometer (Small) [maximum_resistance=100kΩ package=THT]
  R4 = Rotary Potentiometer (Small) [maximum_resistance=100kΩ package=THT]
  R5 = Rotary Potentiometer (Small) [maximum_resistance=100kΩ package=THT]

nets:
  GND: J1.gnd, J2.gnd, J3.gnd, J4.gnd, J5.gnd, Part1.GND, U1.-, R1.leg1, R2.leg1, R3.leg1, R4.leg1, R5.leg1
  N1: J1.pulse, Part1.D5_PWM
  VCC: J2.vcc, J3.vcc, J4.vcc, J5.vcc, U1.+
  N2: J2.pulse, Part1.D6_PWM
  N3: J3.pulse, Part1.D9_PWM
  N4: J4.pulse, Part1.D10_PWM/SS
  N5: J5.pulse, Part1.D3_PWM
  N6: Part1.A0, R2.wiper
  N7: Part1.A1, R1.wiper
  N8: Part1.A2, R3.wiper
  N9: Part1.A3, R4.wiper
  N10: Part1.A4/SDA, R5.wiper
  N11: Part1.5V, R1.leg2, R2.leg2, R3.leg2, R4.leg2, R5.leg2
