# Fritzing sketch 5 Servos (saved by Fritzing 0.8.7b)
breadboards: 1

parts:
  J1 = Basic Servo
  J2 = Basic Servo
  J3 = Basic Servo
  J4 = Basic Servo
  J5 = Basic Servo
  Part1 = Arduino Uno (Rev3)
  U1 = LIPO-1000mAh [package=lipo-1000]

nets:
  GND: J1.gnd, J2.gnd, J3.gnd, J4.gnd, J5.gnd, Part1.GND, U1.-
  N1: J1.pulse, Part1.D5_PWM
  VCC: J2.vcc, J3.vcc, J4.vcc, J5.vcc, U1.+
  N2: J2.pulse, Part1.D6_PWM
  N3: J3.pulse, Part1.D9_PWM
  N4: J4.pulse, Part1.D10_PWM/SS
  N5: J5.pulse, Part1.D3_PWM
